# Fritzing sketch fancontrol_photon_wiring (saved by Fritzing 0.9.3b)
stripboards: 1

parts:
  Part1 = Photon
  J1 = male pin header, 4 pins [form="♂ (male)"]
  J2 = male pin header, 4 pins [form="♂ (male)"]
  J3 = male pin header, 4 pins [form="♂ (male)"]
  J4 = male pin header, 4 pins [form="♂ (male)"]
  J5 = COMPUTER-PERIPHERAL-POWER [package=computer-peripheral-power-ra]
  J6 = male pin header, 3 pins [form="♂ (male)"]
  R1 = Resistor [tolerance=±5% resistance=2.2k package=THT]
  J7 = male pin header, 3 pins [form="♂ (male)"]
  J8 = male pin header, 3 pins [form="♂ (male)"]
  J9 = male pin header, 3 pins [form="♂ (male)"]

nets:
  N1: Part1.A0, J1.pin3
  N2: Part1.A1, J2.pin3
  N3: Part1.A2, J3.pin3
  N4: Part1.A3, J4.pin3
  N5: Part1.RX, J1.pin4
  N6: Part1.TX, J2.pin4
  GND: Part1.GND, J1.pin1, J2.pin1, J3.pin1, J4.pin1, J5.GND, J6.pin1, J7.pin1, J8.pin1, J9.pin1
  N7: Part1.D2, J3.pin4
  N8: Part1.D3, J4.pin4
  N9: Part1.3V3, J6.pin3, J7.pin3, J8.pin3, J9.pin3
  N10: J1.pin2, J2.pin2, J3.pin2, J4.pin2, J5.12V
  N11: J6.pin2, R1.Pin_0, R1.Pin_1, J7.pin2, J8.pin2, J9.pin2

notes:
  Do not connection 5v, as we will power via USB
